// Logisim project Calculadora Hexadecimal.circ as structural Verilog: 1 circuit, main circuit main
module main (
  input  [1:0] in_1,
  input  Op,
  input  _0,
  input  _1,
  input  _2,
  input  _3,
  input  _4,
  input  _5,
  input  _6,
  input  _7,
  input  _8,
  input  _9,
  input  A_10,
  input  B_11,
  input  C_12,
  input  D_13,
  input  E_14,
  input  F_15,
  input  _0_2,
  input  _1_2,
  input  _2_2,
  input  _3_2,
  input  _4_2,
  input  _5_2,
  input  _6_2,
  input  _7_2,
  input  _8_2,
  input  _9_2,
  input  A_10_2,
  input  B_11_2,
  input  C_12_2,
  input  D_13_2,
  input  E_14_2,
  input  F_15_2
);

  wire main_3_carryout, main_4_a, main_4_b, main_4_c, main_4_d, main_4_e, main_4_f, main_4_g;
  wire [3:0] main_1_out_17, main_2_out_17, main_3_s;

  \Conversor_Hexa_para_Binário_main  main_1 (
    ._0(_0), ._1(_1), ._2(_2), ._3(_3), ._4(_4), ._5(_5), ._6(_6), ._7(_7), ._8(_8), ._9(_9), .A_10(A_10),
    .B_11(B_11), .C_12(C_12), .D_13(D_13), .E_14(E_14), .F_15(F_15), .out_17(main_1_out_17));
  \Conversor_Hexa_para_Binário_main  main_2 (
    ._0(_0_2), ._1(_1_2), ._2(_2_2), ._3(_3_2), ._4(_4_2), ._5(_5_2), ._6(_6_2), ._7(_7_2), ._8(_8_2),
    ._9(_9_2), .A_10(A_10_2), .B_11(B_11_2), .C_12(C_12_2), .D_13(D_13_2), .E_14(E_14_2), .F_15(F_15_2),
    .out_17(main_2_out_17));
  ULA_4bits_main main_3 (
    .A(main_1_out_17), .B(main_2_out_17), .Bneg(Op), .in_2(in_1), .S(main_3_s), .CarryOut(main_3_carryout));
  _7_Segment_Display u_7_segment_display_1 (.b(main_3_carryout), .c(main_3_carryout));  // open: g, f, a, e, d, dp
  Display7Segmentos_main main_4 (
    .in_1(main_3_s), .A(main_4_a), .B(main_4_b), .C(main_4_c), .D(main_4_d), .E(main_4_e), .F(main_4_f),
    .G(main_4_g));
  _7_Segment_Display u_7_segment_display_2 (
    .g(main_4_g), .f(main_4_f), .a(main_4_a), .b(main_4_b), .e(main_4_e), .d(main_4_d), .c(main_4_c));  // open: dp

  // Notes on the sheet:
  //   10 e 1 SUBTRAÇÃO
  //   10 e 0 SOMA
  //   01=OR
  //   00=AND
endmodule
