// Logisim project Complemento 2.circ as structural Verilog: 1 circuit, main circuit main
module main (
  input  [3:0] in_1,
  input  Constante,
  input  Constante_2,
  input  Constante_3,
  output [3:0] out_5
);

  wire main_1_ts, main_2_ts, main_3_ts, not_1_out, not_2_out, not_3_out, not_4_out;

  not not_1 (not_1_out, in_1[3]);
  not not_2 (not_2_out, in_1[0]);
  not not_3 (not_3_out, in_1[1]);
  not not_4 (not_4_out, in_1[2]);
  Somador_Completo_main main_1 (.Te(Constante), .A(not_2_out), .B(Constante_2), .S(out_5[0]), .Ts(main_1_ts));
  Somador_Completo_main main_2 (.Te(main_1_ts), .A(not_3_out), .B(Constante_3), .S(out_5[1]), .Ts(main_2_ts));
  Somador_Completo_main main_3 (.Te(main_2_ts), .A(not_4_out), .B(Constante_3), .S(out_5[2]), .Ts(main_3_ts));
  Somador_Completo_main main_4 (.Te(main_3_ts), .A(not_1_out), .B(Constante_3), .S(out_5[3]));  // open: Ts
endmodule
