// Logisim project Conversor Hexa para Binário.circ as structural Verilog: 1 circuit, main circuit main
module main (
  input  _0,
  input  _1,
  input  _2,
  input  _3,
  input  _4,
  input  _5,
  input  _6,
  input  _7,
  input  _8,
  input  _9,
  input  A_10,
  input  B_11,
  input  C_12,
  input  D_13,
  input  E_14,
  input  F_15,
  output [3:0] out_17
);

  or or_1 (out_17[3], _8, _9, A_10, B_11, C_12, D_13, E_14, F_15);
  or or_2 (out_17[2], _4, _5, _6, _7, C_12, D_13, E_14, F_15);
  or or_3 (out_17[1], _2, _3, _6, _7, A_10, B_11, E_14, F_15);
  or or_4 (out_17[0], _1, _3, _5, _7, _9, B_11, D_13, F_15);

  // Notes on the sheet:
  //   Hexadecimal para Binário
endmodule
