// Logisim project Display7Segmentos.circ as structural Verilog: 1 circuit, main circuit main
module main (
  input  [3:0] in_1,
  output A,
  output B,
  output C,
  output D,
  output E,
  output F,
  output G
);

  wire and_1_out, and_2_out, and_3_out, and_4_out, and_5_out, and_6_out, and_7_out, and_8_out, and_9_out,
       and_10_out, and_11_out, and_12_out, and_13_out, and_14_out, and_15_out, and_16_out, and_17_out,
       and_18_out, and_19_out, and_20_out, and_21_out, and_22_out, and_23_out, and_24_out, and_25_out,
       and_26_out, and_27_out, and_28_out, and_29_out, and_30_out, and_31_out, and_32_out, and_33_out,
       and_34_out, and_35_out, and_36_out, and_37_out, and_38_out, and_39_out, and_40_out, not_1_out,
       not_2_out, not_3_out, not_4_out, or_1_out, or_2_out, or_3_out, or_4_out, or_5_out, or_6_out, or_7_out,
       or_8_out, or_9_out, or_10_out, or_11_out, or_12_out, or_13_out, or_14_out, or_15_out, or_16_out,
       or_17_out, or_18_out, or_19_out, or_20_out, or_22_out, or_23_out, or_24_out, or_25_out, or_26_out,
       or_27_out, or_28_out;

  not not_1 (not_1_out, in_1[2]);
  not not_2 (not_2_out, in_1[3]);
  not not_3 (not_3_out, in_1[0]);
  not not_4 (not_4_out, in_1[1]);
  or or_1 (or_1_out, in_1[1], in_1[2]);
  and and_1 (and_1_out, in_1[1], in_1[3]);
  and and_2 (and_2_out, not_2_out, in_1[2], in_1[0]);
  and and_3 (and_3_out, in_1[3], not_1_out, not_4_out);
  and and_4 (and_4_out, in_1[2], in_1[1]);
  and and_5 (and_5_out, not_2_out, in_1[1]);
  and and_6 (and_6_out, not_3_out, in_1[3]);
  and and_7 (and_7_out, not_3_out, not_1_out);
  and and_8 (and_8_out, not_1_out, not_3_out);
  and and_9 (and_9_out, not_1_out, not_4_out);
  and and_10 (and_10_out, not_2_out, in_1[1], in_1[0]);
  and and_11 (and_11_out, not_2_out, in_1[2], not_4_out, not_3_out);
  and and_12 (and_12_out, in_1[3], not_4_out, in_1[2], in_1[0]);
  and and_13 (and_13_out, not_2_out, in_1[2]);
  and and_14 (and_14_out, not_1_out, in_1[3]);
  and and_15 (and_15_out, not_1_out, in_1[0]);
  and and_16 (and_16_out, not_1_out, not_4_out);
  and and_17 (and_17_out, in_1[3], in_1[2], not_4_out, in_1[0]);
  and and_18 (and_18_out, not_2_out, not_1_out, in_1[1]);
  and and_19 (and_19_out, not_2_out, not_1_out, not_3_out);
  and and_20 (and_20_out, in_1[2], in_1[1], not_3_out);
  and and_21 (and_21_out, in_1[3], not_1_out, in_1[0]);
  and and_22 (and_22_out, in_1[3], not_4_out);
  and and_23 (and_23_out, in_1[2], not_4_out, in_1[0]);
  and and_24 (and_24_out, not_3_out, not_1_out);
  and and_25 (and_25_out, in_1[3], or_1_out);
  and and_26 (and_26_out, in_1[1], not_3_out);
  and and_27 (and_27_out, not_2_out, not_4_out);
  or or_2 (or_2_out, in_1[2], not_3_out);
  or or_3 (or_3_out, not_3_out, and_1_out);
  and and_28 (and_28_out, in_1[3], not_1_out);
  or or_4 (or_4_out, in_1[0], not_4_out);
  and and_29 (and_29_out, in_1[3], in_1[1], not_3_out);
  and and_30 (and_30_out, not_2_out, in_1[1]);
  or or_5 (or_5_out, not_3_out, not_1_out);
  and and_31 (and_31_out, in_1[3], not_1_out);
  or or_6 (or_6_out, not_3_out, not_4_out);
  and and_32 (and_32_out, in_1[2], not_4_out);
  or or_7 (or_7_out, in_1[0], not_2_out);
  and and_33 (and_33_out, in_1[3], in_1[1]);
  or or_8 (or_8_out, in_1[2], in_1[0]);
  or or_9 (or_9_out, and_24_out, and_25_out);
  and and_34 (and_34_out, and_30_out, or_5_out);
  and and_35 (and_35_out, and_31_out, or_6_out);
  and and_36 (and_36_out, and_32_out, or_7_out);
  and and_37 (and_37_out, and_33_out, or_8_out);
  or or_10 (or_10_out, and_2_out, and_3_out);
  or or_11 (or_11_out, and_4_out, and_5_out);
  or or_12 (or_12_out, and_6_out, and_7_out);
  or or_13 (or_13_out, and_8_out, and_9_out);
  or or_14 (or_14_out, and_10_out, and_11_out);
  or or_15 (or_15_out, and_13_out, and_14_out);
  or or_16 (or_16_out, and_15_out, and_16_out);
  or or_17 (or_17_out, and_18_out, and_19_out);
  or or_18 (or_18_out, and_20_out, and_21_out);
  or or_19 (or_19_out, and_22_out, and_23_out);
  and and_38 (and_38_out, and_27_out, or_2_out);
  and and_39 (and_39_out, or_3_out, in_1[2]);
  and and_40 (and_40_out, and_28_out, or_4_out);
  or or_20 (or_20_out, or_17_out, or_18_out);
  or or_21 (E, or_9_out, and_26_out);
  or or_22 (or_22_out, and_38_out, and_39_out);
  or or_23 (or_23_out, and_40_out, and_29_out);
  or or_24 (or_24_out, and_34_out, and_35_out);
  or or_25 (or_25_out, and_36_out, and_37_out);
  or or_26 (or_26_out, or_10_out, or_11_out);
  or or_27 (or_27_out, or_14_out, and_12_out);
  or or_28 (or_28_out, or_16_out, and_17_out);
  or or_29 (A, or_26_out, or_12_out);
  or or_30 (B, or_13_out, or_27_out);
  or or_31 (C, or_15_out, or_28_out);
  or or_32 (D, or_20_out, or_19_out);
  or or_33 (F, or_22_out, or_23_out);
  or or_34 (G, or_24_out, or_25_out);
endmodule
