// Logisim project Mux 2x1.circ as structural Verilog: 1 circuit, main circuit main
module main (
  input  A,
  input  a_2,
  input  b,
  output S
);

  wire and_1_out, and_2_out;

  and and_1 (and_1_out, a_2, ~A);  // AND_Gate
  and and_2 (and_2_out, b, A);
  or or_1 (S, and_1_out, and_2_out);
endmodule
