// Logisim project Mux 4x1.circ as structural Verilog: 1 circuit, main circuit main
module main (
  input  [1:0] A_B,
  input  a,
  input  b,
  input  c,
  input  d,
  output S
);

  wire main_1_s, main_2_s;

  Mux_2x1_main main_1 (.a_2(a), .b(b), .A(A_B[0]), .S(main_1_s));
  Mux_2x1_main main_2 (.a_2(c), .b(d), .A(A_B[0]), .S(main_2_s));
  Mux_2x1_main main_3 (.a_2(main_1_s), .b(main_2_s), .A(A_B[1]), .S(S));
endmodule
