// Logisim project ULA 1bit.circ as structural Verilog: 1 circuit, main circuit main
module main (
  input  Bneg,
  input  CarryIN,
  input  [1:0] Sel,
  input  A,
  input  B,
  output out_6,
  output CarryOUT
);

  wire and_1_out, main_1_s, main_2_s, not_1_out;

  not not_1 (not_1_out, B);
  Mux_2x1_main main_1 (.a_2(B), .b(not_1_out), .A(Bneg), .S(main_1_s));
  and and_1 (and_1_out, A, B);
  or or_1 (and_1_out, A, B);
  Somador_Completo_main main_2 (.Te(CarryIN), .A(A), .B(main_1_s), .S(main_2_s), .Ts(CarryOUT));
  Mux_4x1_main main_3 (.a(and_1_out), .b(and_1_out), .c(main_2_s), .A_B(Sel), .S(out_6));  // open: d
endmodule
