// Logisim project ULA 4bits.circ as structural Verilog: 1 circuit, main circuit main
module main (
  input  Bneg,
  input  [1:0] in_2,
  input  [3:0] A,
  input  [3:0] B,
  output [3:0] S,
  output CarryOut
);

  wire main_1_carryout, main_2_carryout, main_3_carryout;

  ULA_1bit_main main_1 (
    .A(A[0]), .B(B[0]), .Bneg(Bneg), .CarryIN(Bneg), .Sel(in_2), .out_6(S[0]), .CarryOUT(main_1_carryout));
  ULA_1bit_main main_2 (
    .A(A[1]), .B(B[1]), .Bneg(Bneg), .CarryIN(main_1_carryout), .Sel(in_2), .out_6(S[1]),
    .CarryOUT(main_2_carryout));
  ULA_1bit_main main_3 (
    .A(A[2]), .B(B[2]), .Bneg(Bneg), .CarryIN(main_2_carryout), .Sel(in_2), .out_6(S[2]),
    .CarryOUT(main_3_carryout));
  ULA_1bit_main main_4 (
    .A(A[3]), .B(B[3]), .Bneg(Bneg), .CarryIN(main_3_carryout), .Sel(in_2), .out_6(S[3]), .CarryOUT(CarryOut));
endmodule
