// Logisim project C2.circ as structural Verilog: 1 circuit, main circuit C2
// C2-3bit
module C2 (
  input  [2:0] in_1,
  output [2:0] out_2
);

  wire not_1_out, not_2_out, not_3_out, sum_1_p4, sum_2_p6;

  not not_1 (not_1_out, in_1[1]);
  not not_2 (not_2_out, in_1[0]);
  not not_3 (not_3_out, in_1[2]);
  // SUM sum_1: pin names not known; wires that end beside it: 1'b0, not_2_out, out_2[0], sum_1_p4
  // SUM sum_2: pin names not known; wires that end beside it: 1'b1, sum_1_p4, not_1_out, 1'b0, out_2[1], sum_2_p6
  // SUM sum_3: pin names not known; wires that end beside it: sum_2_p6, not_3_out, 1'b0, out_2[2]
endmodule
